// Digital circuit dsd_project_digital.dig as structural Verilog
module dsd_project_digital (
  input  pre,
  input  clr,
  input  preset_T,
  input  clear_T
);

  wire avail1, avail2, avail3, avail4, avail5, avail6, avail7, avail8, avail9, button1, button2, button3,
       button4, button5, button6, button7, button8, button9, clk1, clk2, clk3, clk4, clk5, clk6, clk7, clk8,
       clk9, clkAnd1, clkAnd2, clkAnd3, DRAW, gameNotWon, input1, input2, input3, input4, input5, input6,
       input7, input8, input9, nor1, nor2, nor3, nor4, o1, o1_ValidAnd, o2, o2_ValidAnd, o3, o3_ValidAnd, o4,
       o4_ValidAnd, o5, o5_ValidAnd, o6, o6_ValidAnd, o7, o7_ValidAnd, o8, o8_ValidAnd, o9, o9_ValidAnd,
       O_WIN, oColAnd1, oColAnd2, oColAnd3, oDiaAnd1, oDiaAnd2, oOr1, oOr2, oOr3, oRowAnd1, oRowAnd2,
       oRowAnd3, oTurn, tclk, x1, x1_ValidAnd, x2, x2_ValidAnd, x3, x3_ValidAnd, x4, x4_ValidAnd, x5,
       x5_ValidAnd, x6, x6_ValidAnd, x7, x7_ValidAnd, x8, x8_ValidAnd, x9, x9_ValidAnd, X_WIN, xColAnd1,
       xColAnd2, xColAnd3, xDiaAnd1, xDiaAnd2, xOr1, xOr2, xOr3, xRowAnd1, xRowAnd2, xRowAnd3, xTurn;

  LED led_1 (.in(x2));
  LED led_2 (.in(o2));
  LED led_3 (.in(x3));
  LED led_4 (.in(o3));
  LED led_5 (.in(x1));
  LED led_6 (.in(o1));
  _7474 _7474_1 (
    .pin1(clr), .pin2(1'b1), .pin3(x3_ValidAnd), .pin4(pre), .pin5(x3), .pin7(1'b0), .pin9(o3), .pin10(pre),
    .pin11(o3_ValidAnd), .pin12(1'b1), .pin13(clr), .pin14(1'b1));  // open: pin6, pin8
  _7474 _7474_2 (
    .pin1(clr), .pin2(1'b1), .pin3(x2_ValidAnd), .pin4(pre), .pin5(x2), .pin7(1'b0), .pin9(o2), .pin10(pre),
    .pin11(o2_ValidAnd), .pin12(1'b1), .pin13(clr), .pin14(1'b1));  // open: pin6, pin8
  _7474 _7474_3 (
    .pin1(clr), .pin2(1'b1), .pin3(x1_ValidAnd), .pin4(pre), .pin5(x1), .pin7(1'b0), .pin9(o1), .pin10(pre),
    .pin11(o1_ValidAnd), .pin12(1'b1), .pin13(clr), .pin14(1'b1));  // open: pin6, pin8
  Button button_1 (.out(button2));
  Button button_2 (.out(button1));
  Button button_3 (.out(button3));
  and and_1 (o3_ValidAnd, input3, oTurn, avail3);
  and and_2 (input2, button2, gameNotWon);
  and and_3 (o2_ValidAnd, input2, oTurn, avail2);
  and and_4 (x2_ValidAnd, input2, xTurn, avail2);
  nor nor_1 (avail2, x2, o2);
  and and_5 (o1_ValidAnd, input1, oTurn, avail1);
  and and_6 (input3, button3, gameNotWon);
  and and_7 (x3_ValidAnd, input3, xTurn, avail3);
  nor nor_2 (avail3, x3, o3);
  and and_8 (clk2, input2, avail2);
  and and_9 (input1, button1, gameNotWon);
  and and_10 (x1_ValidAnd, input1, xTurn, avail1);
  nor nor_3 (avail1, x1, o1);
  and and_11 (clk3, input3, avail3);
  and and_12 (clk1, input1, avail1);
  LED led_7 (.in(x6));
  LED led_8 (.in(o6));
  LED led_9 (.in(x5));
  LED led_10 (.in(o5));
  LED led_11 (.in(x4));
  LED led_12 (.in(o4));
  _7474 _7474_4 (
    .pin1(clr), .pin2(1'b1), .pin3(x5_ValidAnd), .pin4(pre), .pin5(x5), .pin7(1'b0), .pin9(o5), .pin10(pre),
    .pin11(o5_ValidAnd), .pin12(1'b1), .pin13(clr), .pin14(1'b1));  // open: pin6, pin8
  _7474 _7474_5 (
    .pin1(clr), .pin2(1'b1), .pin3(x4_ValidAnd), .pin4(pre), .pin5(x4), .pin7(1'b0), .pin9(o4), .pin10(pre),
    .pin11(o4_ValidAnd), .pin12(1'b1), .pin13(clr), .pin14(1'b1));  // open: pin6, pin8
  _7474 _7474_6 (
    .pin1(clr), .pin2(1'b1), .pin3(x6_ValidAnd), .pin4(pre), .pin5(x6), .pin7(1'b0), .pin9(o6), .pin10(pre),
    .pin11(o6_ValidAnd), .pin12(1'b1), .pin13(clr), .pin14(1'b1));  // open: pin6, pin8
  Button button_4 (.out(button5));
  Button button_5 (.out(button4));
  Button button_6 (.out(button6));
  LED u_X_WIN (.in(X_WIN));
  and and_13 (o5_ValidAnd, input5, oTurn, avail5);
  and and_14 (x5_ValidAnd, input5, xTurn, avail5);
  and and_15 (o4_ValidAnd, input4, oTurn, avail4);
  and and_16 (x4_ValidAnd, input4, xTurn, avail4);
  LED u_O_WIN (.in(O_WIN));
  and and_17 (o6_ValidAnd, input6, oTurn, avail6);
  and and_18 (x6_ValidAnd, input6, xTurn, avail6);
  nor nor_4 (avail6, x6, o6);
  and and_19 (input5, button5, gameNotWon);
  nor nor_5 (avail5, x5, o5);
  and and_20 (input4, button4, gameNotWon);
  nor nor_6 (avail4, x4, o4);
  and and_21 (input6, button6, gameNotWon);
  and and_22 (clk5, input5, avail5);
  and and_23 (clk4, input4, avail4);
  LED u_DRAW (.in(DRAW));
  and and_24 (clk6, input6, avail6);
  LED led_13 (.in(x8));
  LED led_14 (.in(o8));
  LED led_15 (.in(x7));
  LED led_16 (.in(o7));
  _7476 _7476_1 (
    .pin1(tclk), .pin2(preset_T), .pin3(clear_T), .pin4(1'b1), .pin5(1'b1), .pin6(1'b0), .pin7(1'b0),
    .pin8(1'b0), .pin9(1'b0), .pin12(1'b0), .pin13(1'b0), .pin14(oTurn), .pin15(xTurn), .pin16(1'b1));  // open: pin10, pin11
  LED led_17 (.in(x9));
  LED led_18 (.in(o9));
  _7474 _7474_7 (
    .pin1(clr), .pin2(1'b1), .pin3(x8_ValidAnd), .pin4(pre), .pin5(x8), .pin7(1'b0), .pin9(o8), .pin10(pre),
    .pin11(o8_ValidAnd), .pin12(1'b1), .pin13(clr), .pin14(1'b1));  // open: pin6, pin8
  _7474 _7474_8 (
    .pin1(clr), .pin2(1'b1), .pin3(x9_ValidAnd), .pin4(pre), .pin5(x9), .pin7(1'b0), .pin9(o9), .pin10(pre),
    .pin11(o9_ValidAnd), .pin12(1'b1), .pin13(clr), .pin14(1'b1));  // open: pin6, pin8
  _7474 _7474_9 (
    .pin1(clr), .pin2(1'b1), .pin3(x7_ValidAnd), .pin4(pre), .pin5(x7), .pin7(1'b0), .pin9(o7), .pin10(pre),
    .pin11(o7_ValidAnd), .pin12(1'b1), .pin13(clr), .pin14(1'b1));  // open: pin6, pin8
  Button button_7 (.out(button7));
  Button button_8 (.out(button9));
  Button button_9 (.out(button8));
  and and_25 (DRAW, nor4, gameNotWon);
  and and_26 (o8_ValidAnd, input8, oTurn, avail8);
  or or_1 (tclk, clkAnd1, clkAnd2, clkAnd3);
  and and_27 (nor4, nor3, nor2, nor1);
  and and_28 (o9_ValidAnd, input9, oTurn, avail9);
  and and_29 (input8, button8, gameNotWon);
  and and_30 (x8_ValidAnd, input8, xTurn, avail8);
  nor nor_7 (avail8, x8, o8);
  and and_31 (input7, button7, gameNotWon);
  and and_32 (o7_ValidAnd, input7, oTurn, avail7);
  and and_33 (x7_ValidAnd, input7, xTurn, avail7);
  nor nor_8 (avail7, x7, o7);
  and and_34 (input9, button9, gameNotWon);
  and and_35 (x9_ValidAnd, input9, xTurn, avail9);
  nor nor_9 (avail9, x9, o9);
  and and_36 (clk8, input8, avail8);
  and and_37 (clk7, input7, avail7);
  and and_38 (clk9, input9, avail9);
  or or_2 (clkAnd3, clk1, clk2, clk3);
  or or_3 (clkAnd2, clk4, clk5, clk6);
  or or_4 (clkAnd1, clk7, clk8, clk9);
  nor nor_10 (nor3, avail7, avail8, avail9);
  nor nor_11 (nor2, avail4, avail5, avail6);
  nor nor_12 (nor1, avail1, avail2, avail3);
  or or_5 (O_WIN, oOr3, oOr2, oOr1);
  nor nor_13 (gameNotWon, X_WIN, O_WIN);
  or or_6 (X_WIN, xOr3, xOr2, xOr1);
  or or_7 (oOr3, oDiaAnd2, oDiaAnd1);
  or or_8 (oOr2, oColAnd3, oColAnd2, oColAnd1);
  or or_9 (oOr1, oRowAnd3, oRowAnd2, oRowAnd1);
  or or_10 (xOr2, xColAnd3, xColAnd2, xColAnd1);
  or or_11 (xOr3, xDiaAnd2, xDiaAnd1);
  or or_12 (xOr1, xRowAnd3, xRowAnd2, xRowAnd1);
  and and_39 (oDiaAnd2, o3, o5, o7);
  and and_40 (oDiaAnd1, o1, o5, o9);
  and and_41 (oColAnd3, o3, o6, o9);
  and and_42 (oColAnd2, o2, o5, o8);
  and and_43 (oColAnd1, o1, o4, o7);
  and and_44 (oRowAnd3, o7, o8, o9);
  and and_45 (oRowAnd2, o4, o5, o6);
  and and_46 (oRowAnd1, o1, o2, o3);
  and and_47 (xDiaAnd2, x3, x5, x7);
  and and_48 (xDiaAnd1, x1, x5, x9);
  and and_49 (xColAnd3, x3, x6, x9);
  and and_50 (xColAnd2, x2, x5, x8);
  and and_51 (xColAnd1, x1, x4, x7);
  and and_52 (xRowAnd3, x7, x8, x9);
  and and_53 (xRowAnd2, x4, x5, x6);
  and and_54 (xRowAnd1, x1, x2, x3);

  // Other names for the same wires on the sheet: clrT = clear_T; preT = preset_T

  // Notes on the sheet:
  //   module 3
  //   module 2
  //   module 1
  //   input 2
  //   input 1
  //   input 3
  //   module 5
  //   module 4
  //   module 6
  //   input 5
  //   input 6
  //   input 4
  //   module 8
  //   module 7
  //   module 9
  //   Turn management
  //   input 8
  //   input 7
  //   Draw condition checker
  //   input 9
  //   Game not won yet checker
  //   O player win checker
  //   X player win checker
  //   o - diagnol check
  //   o - column check
  //   o - row check
  //   x - diagnol check
  //   x - column check
  //   x - row check
endmodule
